// Logisim project braile.circ as structural Verilog: 4 circuits, main circuit main
module main (
  input  b1,
  input  b2,
  input  b3,
  input  b4,
  input  in_5,
  input  in_6,
  input  in_7,
  input  in_8
);

  \decodificador_de_padrões  \decodificador_de_padrões_1  (
    .b1(b1), .b2(b2), .b3(b3), .b4(b4));  // open: out_5, out_6, out_7, out_8, out_9

  // Notes on the sheet:
  //   lógica para prefixos
endmodule

module \decodificador_de_padrões  (
  input  b1,
  input  b2,
  input  b3,
  input  b4,
  output out_5,
  output out_6,
  output out_7,
  output out_8,
  output out_9
);

  wire not_1_out, not_2_out, not_3_out, not_4_out, not_5_out, not_6_out, not_7_out, not_8_out, not_9_out,
       not_10_out;

  not not_1 (not_1_out, b2);
  not not_2 (not_2_out, b3);
  not not_3 (not_3_out, b1);
  not not_4 (not_4_out, b4);
  not not_5 (not_5_out, b1);
  not not_6 (not_6_out, b3);
  not not_7 (not_7_out, b1);
  not not_8 (not_8_out, b4);
  not not_9 (not_9_out, b1);
  not not_10 (not_10_out, b1);
  and and_1 (out_5, b4, b3, not_1_out, not_3_out);
  and and_2 (out_6, not_4_out, not_2_out, b2, not_5_out);
  and and_3 (out_7, b4, not_6_out, b2, not_7_out);
  and and_4 (out_8, not_8_out, b3, b2, not_9_out);
  and and_5 (out_9, b4, b3, b2, not_10_out);

  // Notes on the sheet:
  //   Entradas fora do sub
  //   0011 | Saída para o 0 a 9
  //   0100 | A até O, maiúsculo
  //   0101 | P+, maiúsculo
  //   0110 | A até O, minusculo
  //   0111 | P+, minusculo
endmodule

module _0_9 (
  input  ap1,
  output p1,
  output p2,
  output p3,
  output p4,
  output p5,
  output p6
);

  LED u_p1 (.in(p1));
  LED u_p2 (.in(p1));
  xor xor_1 (p1, ap1, ap1);
  LED u_p3 (.in(ap1));
  LED u_p4 (.in(ap1));
  LED u_p5 (.in(ap1));
  LED u_p6 (.in(ap1));

  assign p2 = p1;
  assign p3 = ap1;
  assign p4 = ap1;
  assign p5 = ap1;
  assign p6 = ap1;
endmodule

module levantador_de_pinos_de_prefixo (
  input  in_1,
  input  in_2,
  input  in_3,
  input  in_4,
  input  in_5,
  output out_6,
  output out_7,
  output out_8,
  output out_9,
  output out_10,
  output out_11
);
endmodule
